// Logisim project olaf2.circ as structural Verilog: 6 circuits, main circuit main
module main (
  input  RST
);

  wire CLK_out, cpu_1_get, cpu_1_out, cpu_1_ram_ld, cpu_1_ram_str, cpu_1_rst_out, RST_out;
  wire [6:0] keyboard_1_data;
  wire [23:0] bit_extender_1_out, cpu_1_ip, cpu_1_prnt_data, cpu_1_ram_store, cpu_1_sp, ram_1_data;
  wire [31:0] rom_1_data;

  Clock CLK (.out(CLK_out));
  or u_RST (RST_out, cpu_1_rst_out, RST);
  Pull_Resistor pull_resistor_1 (.node(RST));
  CPU cpu_1 (
    .CLK(CLK_out), .RST_IN(RST), .OPCODE(rom_1_data), .IP(cpu_1_ip), .RST_OUT(cpu_1_rst_out),
    .PRNT_DATA(cpu_1_prnt_data), .IN(bit_extender_1_out), .OUT(cpu_1_out), .GET(cpu_1_get), .SP(cpu_1_sp),
    .RAM_STORE(cpu_1_ram_store), .RAM_LOAD(ram_1_data), .RAM_STR(cpu_1_ram_str), .RAM_LD(cpu_1_ram_ld));
  ROM #(.addrWidth(24), .dataWidth(32)) rom_1 (.addr(cpu_1_ip), .data(rom_1_data), .sel(1'b1));
  RAM #(.addrWidth(24), .dataWidth(24), .bus("separate")) ram_1 (
    .addr(cpu_1_sp), .din(cpu_1_ram_store), .data(ram_1_data), .str(cpu_1_ram_str), .sel(1'b1),
    .clk(CLK_out), .ld(cpu_1_ram_ld), .clr(RST_out));
  Pull_Resistor pull_resistor_2 (.node(ram_1_data));
  TTY #(.rows(16), .cols(64)) tty_1 (.data(cpu_1_prnt_data[6:0]), .clk(CLK_out), .we(cpu_1_out), .clr(RST_out));
  Keyboard keyboard_1 (.clk(CLK_out), .re(cpu_1_get), .clr(RST_out), .data(keyboard_1_data));  // open: avail
  assign bit_extender_1_out = {{17{1'b0}}, keyboard_1_data};  // Bit_Extender bit_extender_1

  // Notes on the sheet:
  //   contents of rom_1 (hex, n*v repeats v):
  //   0 9a 5a1b a19 79a 5a1b 0 439a 4c1b 439a 5a1b 4019 9a 5a1b 2319 2019 539a 4c1b 0 539a 0 34ba 631b 10c
  //   2812 0 539a 0 3dba 631b 10c 2a12 539a 5a1b 3a19 2019 189a 5a1b a19 911 301b 911 2b1b 6219 7919 6219
  //   4c1b 1f c19 1e 9c 648c 3b15 6484 9c 7d 3061 19 3d11 a8c 4515 9d 9c 6485 a84 9c 7d 3061 19 9d a85 9c
  //   7d 3061 19 1e 9c 3d 78 6c 4e12 19 a6c 5712 6f 121 4e11 7a 6f 1e 9c 3d 6e 6c 6212 19 121 5c11 1e 9c
  //   3d e 181 bc 3d 4e 1a1 20d 7213 c 7012 6311 11a 7411 1a 7411 1e
endmodule

module ALU (
  input  [23:0] SOURCE,
  input  [23:0] DEST,
  input  ADD,
  input  SUB,
  input  MUL,
  input  DIV,
  input  SHL,
  input  SHR,
  input  NOT,
  input  AND,
  input  OR,
  input  XOR,
  output CARRY,
  output BORROW,
  output [23:0] OUT,
  output [23:0] MOD,
  output ALU_USED,
  output ZERO
);

  wire not_2_out, not_3_out, not_4_out, not_5_out, not_6_out, not_7_out, not_8_out, not_9_out, not_10_out,
       not_11_out, not_12_out, not_13_out, not_14_out, not_15_out, not_16_out, not_17_out, not_18_out,
       not_19_out, not_20_out, not_21_out, not_22_out, not_23_out, not_24_out, not_25_out;
  wire [4:0] pull_resistor_4_node, pull_resistor_6_node;
  wire [23:0] adder_1_out, and_1_out, controlled_buffer_1_out, controlled_buffer_2_out,
       controlled_buffer_3_out, controlled_buffer_4_out, controlled_buffer_5_out, controlled_buffer_6_out,
       controlled_buffer_7_out, controlled_buffer_8_out, controlled_buffer_15_out, controlled_buffer_17_out,
       controlled_buffer_18_out, controlled_buffer_19_out, divider_1_out, multiplier_1_out, not_1_out,
       or_2_out, pull_resistor_3_node, pull_resistor_5_node, pull_resistor_7_node, pull_resistor_8_node,
       pull_resistor_10_node, shifter_1_out, shifter_2_out, subtractor_1_out, xor_1_out;

  or or_1 (ALU_USED, ADD, SUB, MUL, DIV, SHL, SHR, NOT, AND, OR, XOR);
  assign controlled_buffer_1_out = ADD ? SOURCE : 24'bz;  // Controlled_Buffer controlled_buffer_1
  assign controlled_buffer_2_out = ADD ? DEST : 24'bz;  // Controlled_Buffer controlled_buffer_2
  assign controlled_buffer_3_out = SUB ? SOURCE : 24'bz;  // Controlled_Buffer controlled_buffer_3
  Pull_Resistor pull_resistor_1 (.node(controlled_buffer_3_out));
  assign controlled_buffer_4_out = SUB ? DEST : 24'bz;  // Controlled_Buffer controlled_buffer_4
  Pull_Resistor pull_resistor_2 (.node(controlled_buffer_4_out));
  assign controlled_buffer_5_out = MUL ? SOURCE : 24'bz;  // Controlled_Buffer controlled_buffer_5
  assign controlled_buffer_6_out = MUL ? DEST : 24'bz;  // Controlled_Buffer controlled_buffer_6
  assign controlled_buffer_7_out = DIV ? SOURCE : 24'bz;  // Controlled_Buffer controlled_buffer_7
  assign controlled_buffer_8_out = DIV ? DEST : 24'bz;  // Controlled_Buffer controlled_buffer_8
  Pull_Resistor pull_resistor_3 (.node(pull_resistor_3_node));
  assign pull_resistor_3_node = SHL ? SOURCE : 24'bz;  // Controlled_Buffer controlled_buffer_9
  Pull_Resistor pull_resistor_4 (.node(pull_resistor_4_node));
  assign pull_resistor_4_node = SHL ? DEST[4:0] : 5'bz;  // Controlled_Buffer controlled_buffer_10
  Pull_Resistor pull_resistor_5 (.node(pull_resistor_5_node));
  assign pull_resistor_5_node = SHR ? SOURCE : 24'bz;  // Controlled_Buffer controlled_buffer_11
  Pull_Resistor pull_resistor_6 (.node(pull_resistor_6_node));
  assign pull_resistor_6_node = SHR ? DEST[4:0] : 5'bz;  // Controlled_Buffer controlled_buffer_12
  Pull_Resistor #(.pull(1)) pull_resistor_7 (.node(pull_resistor_7_node));
  assign pull_resistor_7_node = NOT ? SOURCE : 24'bz;  // Controlled_Buffer controlled_buffer_13
  Pull_Resistor pull_resistor_8 (.node(pull_resistor_8_node));
  assign pull_resistor_8_node = AND ? SOURCE : 24'bz;  // Controlled_Buffer controlled_buffer_14
  assign controlled_buffer_15_out = AND ? DEST : 24'bz;  // Controlled_Buffer controlled_buffer_15
  Pull_Resistor pull_resistor_9 (.node(controlled_buffer_15_out));
  Pull_Resistor pull_resistor_10 (.node(pull_resistor_10_node));
  assign pull_resistor_10_node = OR ? SOURCE : 24'bz;  // Controlled_Buffer controlled_buffer_16
  assign controlled_buffer_17_out = OR ? DEST : 24'bz;  // Controlled_Buffer controlled_buffer_17
  Pull_Resistor pull_resistor_11 (.node(controlled_buffer_17_out));
  assign controlled_buffer_18_out = XOR ? SOURCE : 24'bz;  // Controlled_Buffer controlled_buffer_18
  Pull_Resistor pull_resistor_12 (.node(controlled_buffer_18_out));
  assign controlled_buffer_19_out = XOR ? DEST : 24'bz;  // Controlled_Buffer controlled_buffer_19
  Pull_Resistor pull_resistor_13 (.node(controlled_buffer_19_out));
  Adder #(.width(24)) adder_1 (
    .a(controlled_buffer_1_out), .b(controlled_buffer_2_out), .out(adder_1_out), .cout(CARRY));  // open: cin
  Subtractor #(.width(24)) subtractor_1 (
    .a(controlled_buffer_3_out), .b(controlled_buffer_4_out), .out(subtractor_1_out), .bin(1'b0),
    .bout(BORROW));
  Multiplier #(.width(24)) multiplier_1 (
    .a(controlled_buffer_5_out), .b(controlled_buffer_6_out), .out(multiplier_1_out), .cin({24{1'b0}}));  // open: cout
  Divider #(.width(24)) divider_1 (
    .a(controlled_buffer_7_out), .b(controlled_buffer_8_out), .out(divider_1_out), .upper({24{1'b0}}),
    .rem(MOD));
  Shifter #(.width(24)) shifter_1 (.in(pull_resistor_3_node), .\dist (pull_resistor_4_node), .out(shifter_1_out));
  Shifter #(.width(24), .shift("lr")) shifter_2 (
    .in(pull_resistor_5_node), .\dist (pull_resistor_6_node), .out(shifter_2_out));
  assign not_1_out = ~pull_resistor_7_node;  // NOT_Gate not_1, 24 bits wide
  assign and_1_out = pull_resistor_8_node & controlled_buffer_15_out;  // AND_Gate and_1, 24 bits wide
  assign or_2_out = pull_resistor_10_node | controlled_buffer_17_out;  // OR_Gate or_2, 24 bits wide
  assign xor_1_out = controlled_buffer_18_out ^ controlled_buffer_19_out;  // XOR_Gate xor_1, 24 bits wide
  Pull_Resistor pull_resistor_14 (.node(adder_1_out));
  Pull_Resistor pull_resistor_15 (.node(multiplier_1_out));
  Pull_Resistor pull_resistor_16 (.node(divider_1_out));
  Pull_Resistor pull_resistor_17 (.node(shifter_1_out));
  Pull_Resistor pull_resistor_18 ();  // open: node
  Pull_Resistor pull_resistor_19 (.node(not_1_out));
  Pull_Resistor pull_resistor_20 (.node(and_1_out));
  Pull_Resistor pull_resistor_21 (.node(or_2_out));
  Pull_Resistor pull_resistor_22 (.node(xor_1_out));
  Pull_Resistor pull_resistor_23 (.node(CARRY));
  Pull_Resistor pull_resistor_24 (.node(BORROW));
  ExactlyOne xor_2[23:0] (
    .out(OUT), .in0(adder_1_out), .in1(subtractor_1_out), .in2(multiplier_1_out), .in3(divider_1_out),
    .in4(shifter_1_out), .in5(shifter_2_out), .in6(not_1_out), .in7(and_1_out), .in8(or_2_out),
    .in9(xor_1_out));
  Pull_Resistor pull_resistor_25 (.node(MOD));
  Pull_Resistor pull_resistor_26 (.node(OUT));
  not not_2 (not_2_out, OUT[0]);
  not not_3 (not_3_out, OUT[1]);
  not not_4 (not_4_out, OUT[2]);
  not not_5 (not_5_out, OUT[3]);
  not not_6 (not_6_out, OUT[4]);
  not not_7 (not_7_out, OUT[5]);
  not not_8 (not_8_out, OUT[6]);
  not not_9 (not_9_out, OUT[7]);
  not not_10 (not_10_out, OUT[8]);
  not not_11 (not_11_out, OUT[9]);
  not not_12 (not_12_out, OUT[10]);
  not not_13 (not_13_out, OUT[11]);
  and and_2 (ZERO, not_2_out, not_3_out, not_4_out, not_5_out, not_6_out, not_7_out, not_8_out, not_9_out, not_10_out, not_11_out, not_12_out, not_13_out, not_14_out, not_15_out, not_16_out, not_17_out, not_18_out, not_19_out, not_20_out, not_21_out, not_22_out, not_23_out, not_24_out, not_25_out);
  not not_14 (not_14_out, OUT[12]);
  not not_15 (not_15_out, OUT[13]);
  not not_16 (not_16_out, OUT[14]);
  not not_17 (not_17_out, OUT[15]);
  not not_18 (not_18_out, OUT[16]);
  not not_19 (not_19_out, OUT[17]);
  not not_20 (not_20_out, OUT[18]);
  not not_21 (not_21_out, OUT[19]);
  not not_22 (not_22_out, OUT[20]);
  not not_23 (not_23_out, OUT[21]);
  not not_24 (not_24_out, OUT[22]);
  not not_25 (not_25_out, OUT[23]);
endmodule

module CPU (
  input  [23:0] IN,
  input  CLK,
  input  RST_IN,
  input  [31:0] OPCODE,
  input  [23:0] RAM_LOAD,
  output GET,
  output OUT,
  output RST_OUT,
  output [23:0] PRNT_DATA,
  output RAM_LD,
  output RAM_STR,
  output [23:0] RAM_STORE,
  output [23:0] IP,
  output [23:0] SP
);

  wire alu_1_alu_used, alu_1_borrow, alu_1_carry, alu_1_zero, controlled_buffer_2_out, decoder_1_out1,
       decoder_1_out2, decoder_1_out3, decoder_1_out4, decoder_1_out5, decoder_1_out6, decoder_1_out7,
       decoder_1_out8, decoder_1_out9, decoder_1_out10, decoder_1_out11, decoder_1_out12, decoder_1_out13,
       decoder_1_out14, decoder_1_out15, decoder_1_out17, decoder_1_out18, decoder_1_out19, decoder_1_out20,
       decoder_1_out21, decoder_1_out22, decoder_1_out23, decoder_1_out25, decoder_1_out26, decoder_1_out27,
       decoder_1_out28, decoder_1_out29, decoder_1_out30, DIV_out, flags_1_jmp_out, HAS_VALLUE_out,
       i_o_1_prnt, JMP_out, MOV_2_out, MOV_out, nor_1_out, not_1_out, not_2_out, not_3_out, not_4_out,
       not_5_out, PSH_out, RST_2_out, RST_out_2, SUB_out, TST_out;
  wire [2:0] flags_1_ip_reg, i_o_1_data_reg, REG_out;
  wire [23:0] alu_1_mod, alu_1_out, controlled_buffer_3_out, controlled_buffer_4_out,
       controlled_buffer_5_out, controlled_buffer_6_out, controlled_buffer_7_out, controlled_buffer_8_out,
       controlled_buffer_9_out, controlled_buffer_10_out, DST_out, i_o_1__in, or_1_out, pull_resistor_2_node,
       pull_resistor_4_node, regs_1_ra, regs_1_rb, regs_1_rc, regs_1_rd, regs_1_rdi, regs_1_rsi, regs_1_sp,
       VAL_out;

  Decoder #(.select(5), .enable("false")) decoder_1 (
    .out1(decoder_1_out1), .out2(decoder_1_out2), .out3(decoder_1_out3), .out4(decoder_1_out4),
    .out5(decoder_1_out5), .out6(decoder_1_out6), .out7(decoder_1_out7), .out8(decoder_1_out8),
    .out9(decoder_1_out9), .out10(decoder_1_out10), .out11(decoder_1_out11), .out12(decoder_1_out12),
    .out13(decoder_1_out13), .out14(decoder_1_out14), .out15(decoder_1_out15), .out17(decoder_1_out17),
    .out18(decoder_1_out18), .out19(decoder_1_out19), .out20(decoder_1_out20), .out21(decoder_1_out21),
    .out22(decoder_1_out22), .out23(decoder_1_out23), .out24(GET), .out25(decoder_1_out25),
    .out26(decoder_1_out26), .out27(decoder_1_out27), .out28(decoder_1_out28), .out29(decoder_1_out29),
    .out30(decoder_1_out30), .out31(RST_OUT), .sel(OPCODE[4:0]));  // open: out0, out16
  or RST (RST_out_2, RST_OUT, RST_IN);
  Pull_Resistor pull_resistor_1 (.node(RAM_LOAD));
  or SUB (SUB_out, decoder_1_out2, decoder_1_out13, decoder_1_out12);
  or TST (TST_out, decoder_1_out12, decoder_1_out13);
  or JMP (JMP_out, decoder_1_out17, decoder_1_out30, decoder_1_out27);
  or PSH (PSH_out, decoder_1_out27, decoder_1_out28);
  assign REG_out = flags_1_ip_reg | i_o_1_data_reg | OPCODE[7:5];  // OR_Gate REG, 3 bits wide
  Pull_Resistor pull_resistor_2 (.node(pull_resistor_2_node));
  assign pull_resistor_2_node = RST_2_out ? OPCODE[31:8] : 24'bz;  // Controlled_Buffer controlled_buffer_1
  or RST_2 (RST_2_out, decoder_1_out26, flags_1_jmp_out);
  or HAS_VALLUE (HAS_VALLUE_out, OPCODE[8], OPCODE[9], OPCODE[10], OPCODE[11], OPCODE[12], OPCODE[13], OPCODE[14], OPCODE[15], 1'b0);
  FLAGS flags_1 (
    .JMP(JMP_out), .JEQ(decoder_1_out18), .JNE(decoder_1_out19), .JBT(decoder_1_out20),
    .JST(decoder_1_out21), .JBE(decoder_1_out22), .JLE(decoder_1_out23), .BORROW(alu_1_borrow),
    .ZERO(alu_1_zero), .IP_REG(flags_1_ip_reg), .JMP_OUT(flags_1_jmp_out), .TEST(TST_out), .CLK(CLK),
    .RST(RST_out_2), .CARRY(alu_1_carry));
  or MOV (MOV_out, decoder_1_out26, flags_1_jmp_out, decoder_1_out14, MOV_2_out, GET);
  assign VAL_out = pull_resistor_2_node | i_o_1__in | or_1_out | RAM_LOAD;  // OR_Gate VAL, 24 bits wide
  assign controlled_buffer_2_out = decoder_1_out25 ? HAS_VALLUE_out : 1'bz;  // Controlled_Buffer controlled_buffer_2
  not not_1 (not_1_out, decoder_1_out13);
  assign controlled_buffer_3_out = not_1_out ? OPCODE[31:8] : 24'bz;  // Controlled_Buffer controlled_buffer_3
  or DIV (DIV_out, decoder_1_out4, decoder_1_out5);
  I_O i_o_1 (.GET(GET), .OUT(decoder_1_out25), .IN(IN), ._IN(i_o_1__in), .PRNT(i_o_1_prnt), .DATA_REG(i_o_1_data_reg));
  REGS regs_1 (
    .CLK(CLK), .RST(RST_out_2), .REG(REG_out), .VAL(VAL_out), .MOV(MOV_out), .RA(regs_1_ra), .RB(regs_1_rb),
    .RC(regs_1_rc), .RD(regs_1_rd), .SP(regs_1_sp), .PUSH(PSH_out), .POP(decoder_1_out29),
    .RET(decoder_1_out30), .RDI(regs_1_rdi), .RSI(regs_1_rsi), .IP(IP));
  Pull_Resistor pull_resistor_3 (.node(controlled_buffer_2_out));
  Pull_Resistor pull_resistor_4 (.node(pull_resistor_4_node));
  assign DST_out = pull_resistor_4_node | controlled_buffer_3_out;  // OR_Gate DST, 24 bits wide
  Pull_Resistor pull_resistor_5 (.node(controlled_buffer_3_out));
  assign controlled_buffer_4_out = not_2_out ? controlled_buffer_5_out : 24'bz;  // Controlled_Buffer controlled_buffer_4
  Pull_Resistor pull_resistor_6 (.node(controlled_buffer_4_out));
  assign controlled_buffer_5_out = i_o_1_prnt ? regs_1_rd : 24'bz;  // Controlled_Buffer controlled_buffer_5
  not not_2 (not_2_out, controlled_buffer_2_out);
  assign controlled_buffer_6_out = controlled_buffer_2_out ? OPCODE[31:8] : 24'bz;  // Controlled_Buffer controlled_buffer_6
  Pull_Resistor pull_resistor_7 (.node(controlled_buffer_6_out));
  ALU alu_1 (
    .SOURCE(RAM_STORE), .DEST(DST_out), .ADD(decoder_1_out1), .SUB(SUB_out), .MUL(decoder_1_out3),
    .DIV(DIV_out), .SHL(decoder_1_out6), .SHR(decoder_1_out7), .NOT(decoder_1_out9), .AND(decoder_1_out10),
    .OR(decoder_1_out11), .XOR(decoder_1_out8), .CARRY(alu_1_carry), .BORROW(alu_1_borrow),
    .ZERO(alu_1_zero), .OUT(alu_1_out), .MOD(alu_1_mod), .ALU_USED(alu_1_alu_used));
  not not_3 (not_3_out, TST_out);
  assign PRNT_DATA = controlled_buffer_4_out | controlled_buffer_6_out;  // OR_Gate PRT, 24 bits wide
  Pull_Resistor pull_resistor_8 (.node(PRNT_DATA));
  and MOV_2 (MOV_2_out, alu_1_alu_used, not_3_out);
  assign controlled_buffer_7_out = decoder_1_out5 ? alu_1_mod : 24'bz;  // Controlled_Buffer controlled_buffer_7
  Pull_Resistor pull_resistor_9 (.node(controlled_buffer_7_out));
  Multiplexer #(.select(3), .width(24), .enable("false")) multiplexer_1 (
    .in0(regs_1_ra), .in1(regs_1_rb), .in2(regs_1_rc), .in3(regs_1_rd), .in4(regs_1_rdi), .in5(regs_1_rsi),
    .in6(IP), .in7(regs_1_sp), .out(RAM_STORE), .sel(REG_out));
  nor nor_1 (nor_1_out, decoder_1_out14, decoder_1_out15);
  assign controlled_buffer_8_out = nor_1_out ? regs_1_sp : 24'bz;  // Controlled_Buffer controlled_buffer_8
  Multiplexer #(.select(3), .width(24)) multiplexer_2 (
    .in0(regs_1_ra), .in1(regs_1_rb), .in2(regs_1_rc), .in3(regs_1_rd), .in4(regs_1_rdi), .in5(regs_1_rsi),
    .in6(IP), .in7(regs_1_sp), .out(pull_resistor_4_node), .sel(OPCODE[10:8]), .en(decoder_1_out13));
  not not_4 (not_4_out, decoder_1_out5);
  assign controlled_buffer_9_out = not_4_out ? alu_1_out : 24'bz;  // Controlled_Buffer controlled_buffer_9
  Pull_Resistor pull_resistor_10 (.node(controlled_buffer_9_out));
  assign or_1_out = controlled_buffer_7_out | controlled_buffer_9_out;  // OR_Gate or_1, 24 bits wide
  Pull_Resistor pull_resistor_11 (.node(or_1_out));
  or or_2 (OUT, PRNT_DATA[0], PRNT_DATA[1], PRNT_DATA[2], PRNT_DATA[3], PRNT_DATA[4], PRNT_DATA[5], PRNT_DATA[6]);
  not not_5 (not_5_out, nor_1_out);
  assign controlled_buffer_10_out = not_5_out ? regs_1_rb : 24'bz;  // Controlled_Buffer controlled_buffer_10
  Pull_Resistor pull_resistor_12 (.node(controlled_buffer_8_out));
  or or_3 (RAM_LD, decoder_1_out29, decoder_1_out14, decoder_1_out30);
  or or_4 (RAM_STR, PSH_out, decoder_1_out15);
  Pull_Resistor pull_resistor_13 (.node(RAM_STORE));
  Pull_Resistor pull_resistor_14 (.node(controlled_buffer_10_out));
  assign SP = controlled_buffer_10_out | controlled_buffer_8_out;  // OR_Gate or_5, 24 bits wide

  // Notes on the sheet:
  //   RAM_LOAD: pull=down
  //   IN: pull=down
  //   OPCODE: pull=down
  //   NOP
  //   ADD
  //   SUB
  //   MUL
  //   DIV
  //   MOD
  //   SHL
  //   SHR
  //   XOR
  //   NOT
  //   AND
  //   OR
  //   TEST
  //   TSTR
  //   LOAD
  //   STOR
  //   JMP
  //   JEQ
  //   JNE
  //   JBT
  //   JST
  //   JBE
  //   JLE
  //   GET
  //   OUT
  //   MOV
  //   CALL
  //   PUSH
  //   POP
  //   RET
  //   RST
  //   SRC
endmodule

module REGS (
  input  CLK,
  input  RST,
  input  [2:0] REG,
  input  [23:0] VAL,
  input  MOV,
  input  PUSH,
  input  POP,
  input  RET,
  output [23:0] RA,
  output [23:0] RB,
  output [23:0] RC,
  output [23:0] RD,
  output [23:0] RDI,
  output [23:0] RSI,
  output [23:0] IP,
  output [23:0] SP
);

  wire decoder_1_out0, decoder_1_out1, decoder_1_out2, decoder_1_out3, decoder_1_out4, decoder_1_out5,
       decoder_1_out6, decoder_1_out7, nor_1_out, not_1_out, not_2_out, not_3_out, not_4_out, or_1_out,
       or_4_out, or_6_out, xor_1_out;
  wire [2:0] controlled_buffer_3_out, controlled_buffer_4_out, or_3_out;
  wire [23:0] adder_1_out, adder_2_out, controlled_buffer_1_out, controlled_buffer_2_out,
       controlled_buffer_6_out, or_2_out, or_5_out, pull_resistor_7_node, pull_resistor_8_node,
       subtractor_1_out;

  not not_1 (not_1_out, RET);
  Decoder #(.select(3), .disabled(0)) decoder_1 (
    .out0(decoder_1_out0), .out1(decoder_1_out1), .out2(decoder_1_out2), .out3(decoder_1_out3),
    .out4(decoder_1_out4), .out5(decoder_1_out5), .out6(decoder_1_out6), .out7(decoder_1_out7),
    .sel(or_3_out), .en(or_1_out));
  or or_1 (or_1_out, MOV, POP);
  assign controlled_buffer_1_out = not_1_out ? VAL : 24'bz;  // Controlled_Buffer controlled_buffer_1
  Pull_Resistor pull_resistor_1 (.node(controlled_buffer_1_out));
  Adder #(.width(24)) adder_1 (.a(VAL), .b({24{1'b1}}), .out(adder_1_out), .cin(1'b0));  // open: cout
  assign controlled_buffer_2_out = RET ? adder_1_out : 24'bz;  // Controlled_Buffer controlled_buffer_2
  Pull_Resistor pull_resistor_2 (.node(controlled_buffer_2_out));
  assign controlled_buffer_3_out = not_2_out ? REG : 3'bz;  // Controlled_Buffer controlled_buffer_3
  Pull_Resistor pull_resistor_3 (.node(controlled_buffer_3_out));
  not not_2 (not_2_out, PUSH);
  assign controlled_buffer_4_out = PUSH ? 3'b110 : 3'bz;  // Controlled_Buffer controlled_buffer_4
  Pull_Resistor pull_resistor_4 (.node(controlled_buffer_4_out));
  assign or_2_out = controlled_buffer_1_out | controlled_buffer_2_out;  // OR_Gate or_2, 24 bits wide
  Register #(.width(24), .trigger("falling")) u_RA (.D(or_2_out), .en(decoder_1_out0), .Q(RA), .clk(CLK), .clr(RST));
  assign or_3_out = controlled_buffer_3_out | controlled_buffer_4_out;  // OR_Gate or_3, 3 bits wide
  Register #(.width(24), .trigger("falling")) u_RB (.D(or_2_out), .en(decoder_1_out1), .Q(RB), .clk(CLK), .clr(RST));
  Pull_Resistor pull_resistor_5 (.node(RET));
  Register #(.width(24), .trigger("falling")) u_RC (.D(or_2_out), .en(decoder_1_out2), .Q(RC), .clk(CLK), .clr(RST));
  or or_4 (or_4_out, POP, RET);
  Register #(.width(24), .trigger("falling")) u_RDI (.D(or_2_out), .en(decoder_1_out4), .Q(RDI), .clk(CLK), .clr(RST));
  Register #(.width(24), .trigger("falling")) u_RD (.D(or_2_out), .en(decoder_1_out3), .Q(RD), .clk(CLK), .clr(RST));
  Register #(.width(24), .trigger("falling")) u_RSI (.D(or_2_out), .en(decoder_1_out5), .Q(RSI), .clk(CLK), .clr(RST));
  not not_3 (not_3_out, decoder_1_out6);
  Subtractor #(.width(24)) subtractor_1 (.a({24{1'b1}}), .b(SP), .out(subtractor_1_out), .bin(1'b0));  // open: bout
  Adder #(.width(24)) adder_2 (.a({24{1'b1}}), .b(SP), .out(adder_2_out), .cin(1'b0));  // open: cout
  Pull_Resistor pull_resistor_6 (.node(IP));
  nor nor_1 (nor_1_out, PUSH, or_4_out);
  Counter #(.width(24), .max('hffffff), .ongoal("stay"), .trigger("falling")) u_IP (
    .load(decoder_1_out6), .D(or_2_out), .count(not_3_out), .Q(IP), .clk(not_4_out), .clr(RST));  // open: carry
  not not_4 (not_4_out, xor_1_out);
  xor xor_1 (xor_1_out, RET, CLK);
  Pull_Resistor pull_resistor_7 (.node(pull_resistor_7_node));
  assign pull_resistor_7_node = PUSH ? subtractor_1_out : 24'bz;  // Controlled_Buffer controlled_buffer_5
  assign controlled_buffer_6_out = or_4_out ? adder_2_out : 24'bz;  // Controlled_Buffer controlled_buffer_6
  Pull_Resistor pull_resistor_8 (.node(pull_resistor_8_node));
  assign pull_resistor_8_node = nor_1_out ? or_2_out : 24'bz;  // Controlled_Buffer controlled_buffer_7
  Pull_Resistor pull_resistor_9 (.node(pull_resistor_7_node));
  assign or_5_out = pull_resistor_8_node | pull_resistor_7_node | controlled_buffer_6_out;  // OR_Gate or_5, 24 bits wide
  Pull_Resistor pull_resistor_10 (.node(controlled_buffer_6_out));
  or or_6 (or_6_out, decoder_1_out7, or_4_out, PUSH, RET);
  Pull_Resistor pull_resistor_11 (.node(controlled_buffer_6_out));
  Register #(.width(24), .trigger("falling")) u_SP (.D(or_5_out), .en(or_6_out), .Q(SP), .clk(CLK), .clr(RST));

  // Notes on the sheet:
  //   PUSH: pull=down
  //   RET: pull=down
  //   RST: pull=down
  //   CLK: pull=down
  //   MOV: pull=down
  //   POP: pull=down
  //   REG: pull=down
endmodule

module FLAGS (
  input  TEST,
  input  CLK,
  input  RST,
  input  JMP,
  input  JEQ,
  input  JNE,
  input  JBT,
  input  BORROW,
  input  JST,
  input  CARRY,
  input  JBE,
  input  ZERO,
  input  JLE,
  output [2:0] IP_REG,
  output JMP_OUT
);

  wire JBE_2_out, JBE_out, JBT_out, JEQ_out, JLE_2_out, JLE_out, JNE_out, JST_out, not_1_out, not_2_out,
       not_3_out, or_1_out, or_2_out, register_1_q, register_3_q;

  not not_1 (not_1_out, register_3_q);
  not not_2 (not_2_out, register_1_q);
  and u_JBT (JBT_out, not_2_out, JBT);
  and u_JST (JST_out, register_1_q, JST);
  not not_3 (not_3_out, register_1_q);
  and u_JBE (JBE_out, not_3_out, JBE);
  and JBE_2 (JBE_2_out, register_1_q, JLE);
  and u_JLE (JLE_out, register_1_q, JBE);
  and JLE_2 (JLE_2_out, register_1_q, JLE);
  and u_JEQ (JEQ_out, JEQ, register_3_q);
  and u_JNE (JNE_out, JNE, not_1_out);
  or or_1 (or_1_out, JBE_out, JLE_out);
  or or_2 (or_2_out, JBE_2_out, JLE_2_out);
  Pull_Resistor pull_resistor_1 (.node(IP_REG));
  assign IP_REG = JMP_OUT ? 3'b110 : 3'bz;  // Controlled_Buffer controlled_buffer_1
  or or_3 (JMP_OUT, JMP, JEQ_out, JNE_out, JBT_out, JST_out, or_1_out, or_2_out);
  Register #(.width(1), .trigger("falling")) register_1 (.D(BORROW), .en(TEST), .Q(register_1_q), .clk(CLK), .clr(RST));
  Register #(.width(1), .trigger("falling")) register_2 (.D(CARRY), .en(TEST), .clk(CLK), .clr(RST));  // open: Q
  Register #(.width(1), .trigger("falling")) register_3 (.D(ZERO), .en(TEST), .Q(register_3_q), .clk(CLK), .clr(RST));

  // Notes on the sheet:
  //   BORROW: pull=down
  //   JNE: pull=down
  //   JMP: pull=down
  //   JBE: pull=down
  //   CARRY: pull=down
  //   JBT: pull=down
  //   TEST: pull=down
  //   JST: pull=down
  //   CLK: pull=down
  //   JEQ: pull=down
  //   JLE: pull=down
  //   ZERO: pull=down
  //   RST: pull=down
endmodule

module I_O (
  input  [23:0] IN,
  input  GET,
  input  OUT,
  output [23:0] _IN,
  output PRNT,
  output [2:0] DATA_REG
);

  Pull_Resistor pull_resistor_1 (.node(_IN));
  assign _IN = GET ? IN : 24'bz;  // Controlled_Buffer controlled_buffer_1
  Pull_Resistor pull_resistor_2 (.node(DATA_REG));
  assign DATA_REG = OUT ? 3'b011 : 3'bz;  // Controlled_Buffer controlled_buffer_2

  assign PRNT = OUT;

  // Notes on the sheet:
  //   GET: pull=down
  //   OUT: pull=down
  //   IN: pull=down
endmodule
